# Fritzing sketch system_module (saved by Fritzing 0.9.3b)
breadboards: 2

parts:
  Raspberry_Pi_1 = Raspberry Pi 3 [part_number=RPI-3-V1.2]
  GY2 = MPU-6050 Board GY-521 [form="♀ (female)" package=THT]
  U1 = LCD-16X2 [package=lcd-16x2]
  R2 = Trimmer Potentiometer [maximum_resistance=10kΩ package=THT]

nets:
  N1: Raspberry_Pi_1.3v3, GY2.pin1
  N2: Raspberry_Pi_1.GPIO2, GY2.pin4
  N3: Raspberry_Pi_1.GPIO3, GY2.pin3
  GND: Raspberry_Pi_1.GND, GY2.pin2, U1.VSS, U1.R_W, U1.K, R2.leg1
  N4: Raspberry_Pi_1.GIPO7, U1.DB7
  N5: Raspberry_Pi_1.GIPO8, U1.DB6
  N6: Raspberry_Pi_1.GIPO25, U1.DB5
  N7: Raspberry_Pi_1.GIPO24, U1.DB4
  N8: Raspberry_Pi_1.GIPO23, U1.E
  N9: Raspberry_Pi_1.GIPO18, U1.RS
  5V: Raspberry_Pi_1.5V, U1.VDD, U1.A, R2.leg2
  N10: U1.VO, R2.wiper

notes:
  Fritizing Representation of drone flight regulator
  System Features an MPU-6050 component for measuring the temperature, altitude, acceleration and directions in which the system is moving.
  The 16x2 LCD, is used for displaying the above information, so the user can see.
  Feature components such as
  1. multi color leds can be featured to display specific colors depending on the specific condition.
  2.Fans, can be incuded when creating the diven system.

custom parts:
  MPU-6050 Board GY-521: Acelerometro y Giroscopio MPU-6050 Board GY-521
